// Logisim project SelectionSort.circ as structural Verilog: 1 circuit, main circuit main
module main (
  input  done,
  input  [7:0] data,
  input  data_av
);

  wire clk_out, not_1_out, rst_out, undriven_2, undriven_4;
  wire [7:0] ram_1_data, undriven, undriven_3;

  Clock clk (.out(clk_out));
  Button rst (.out(rst_out));
  not not_1 (not_1_out, undriven_4);
  RAM ram_1 (.addr(undriven_3), .data(ram_1_data), .sel(undriven_2), .clk(clk_out), .ld(undriven_4));  // open: clr
  assign ram_1_data = not_1_out ? undriven : 8'bz;  // Controlled_Buffer controlled_buffer_1

  // Notes on the sheet:
  //   data_in
  //   data_out
endmodule
